# Fritzing sketch 4Wire Reference Diagram (saved by Fritzing 0.9.3b)

parts:
  Part1 = Arduino Prototyping Shield
  J1 = screw terminal, 2 pins
  J2 = Screw terminal - 2 pins [package=THT]

nets:
  N1: Part1.D12, J1.pin1
  N2: Part1.N$105, J2.pin2
  N3: Part1.N$321, J2.pin1
  N4: Part1.N$397, J1.pin2
